# Fritzing sketch BasicRefrigeratorSystem (saved by Fritzing 0.8.7b)
breadboards: 1

parts:
  Componente1 = Arduino Uno (Rev3)
  T1 = LM35 Temperature Sensor [package="TO92 [THT]"]
  U1 = LCD-16X2 [package=lcd-16x2]
  R1 = Resistor [tolerance=±5% resistance=220 package=THT]
  R2 = Resistor [tolerance=±5% resistance=220 package=THT]
  R3 = Resistor [package="2010 [SMD]"]
  KY-2 = Keyes Relay [package=THT]
  F1 = Fan - Ventilador [package=THT]
  Part3 = Lilypad Battery Connect

nets:
  N1: Componente1.A2, T1.Vout
  N2: Componente1.D12/MISO, U1.RS
  N3: Componente1.D13/SCK, U1.E
  N4: Componente1.D2, KY-2.signal
  N5: Componente1.D4, U1.DB7
  N6: Componente1.D5_PWM, U1.DB6
  N7: Componente1.D6_PWM, U1.DB5
  N8: Componente1.D7, U1.DB4
  5V: Componente1.5V, T1.+Vs, U1.VDD, R2.Pin_1, KY-2.power
  GND: Componente1.GND, T1.GND, U1.VSS, U1.R_W, U1.K, R1.Pin_1, KY-2.ground
  N9: U1.VO, R1.Pin_0
  N10: U1.A, R3.Pin_0
  N11: R2.Pin_0, R3.Pin_1
  N12: KY-2.C, Part3.+
  N13: KY-2.NO, F1.5V
  N14: F1.GND, Part3.-

custom parts:
  Keyes Relay: The Keyes 5V relay module is suitable for SCM development, home appliance control. It uses a 5V~12V TIL control signal which can control DC / AC signal.
  Fan - Ventilador: Ventilador de 2 pines, se encuentra comunmente en computadoras de escritorio
